// Digital circuit RV5-PROCESSOR.dig as structural Verilog
module RV5_PROCESSOR (
  input  clock
);

  wire alu_bsel, branch_sel, dm_mem_addr, dm_mem_rdata, dm_mem_wdata, dm_mem_wen, haltreq, jal_sel, jalr_sel,
       jump_progbuf, ld_signext, mem_b, mem_h, memren, memwen, memwen_t, npc, npc_t, regwen, regwen_t,
       resumereq, rv5_alu_1_p5, rv5_alu_1_p6, rv5_alu_1_p7, rv5_pcu_1_p5;
  wire [1:0] alu_asel, wb_sel;
  wire [2:0] funct3, imm_sel;
  wire [3:0] alu_op;
  wire [4:0] rd, rd_t, rs1, rs1_t;
  wire [6:0] opcode;
  wire [11:0] funct12;
  wire [31:0] multiplexer_1_out, pc, R_rs1, rv5_alu_1_p2, rv5_gpr_1_rb, rv5_memory_1_p14, rv5_pcu_1_p4,
       rv5_pcu_1_p6, wb, wb_t;
  wire [31:2] add_1_s;

  // RV5_PCU rv5_pcu_1: pin names not known; wires that end beside it: jalr_sel, clock, npc_t, rv5_pcu_1_p4, rv5_pcu_1_p5, rv5_pcu_1_p6, pc, npc
  // RV5_DEBUG_ZICSR rv5_debug_zicsr_1: pin names not known; wires that end beside it: clock, dm_mem_rdata, R_rs1, regwen, memwen, rd, rs1, wb, pc, npc, opcode, funct3, funct12, haltreq, resumereq, jump_progbuf, dm_mem_wdata, dm_mem_wen, dm_mem_addr, regwen_t, memwen_t, rd_t, rs1_t, wb_t, npc_t
  RV5_CONTROL_LOGIC rv5_control_logic_1 (
    .opcode(opcode), .funct3(funct3), .funct12(funct12), .imm_sel(imm_sel), .reg_wen(regwen),
    .mem_wen(memwen), .mem_ren(memren), .mem_b(mem_b), .mem_h(mem_h), .ld_signext(ld_signext),
    .alu_asel(alu_asel), .alu_bsel(alu_bsel), .alu_op(alu_op), .branch_sel(branch_sel), .jal_sel(jal_sel),
    .jalr_sel(jalr_sel), .wb_sel(wb_sel));
  RV5_IMM_GEN rv5_imm_gen_1 (.INSTR_32({funct12, rs1, funct3, rd, opcode}), .imm_sel(imm_sel), .imm(rv5_pcu_1_p6));
  RV5_GPR rv5_gpr_1 (
    .RS1(rs1_t), .RS2(funct12[4:0]), .D_in(wb_t), .clk(clock), .RD(rd_t), .WEN(regwen_t), .RA(R_rs1),
    .RB(rv5_gpr_1_rb));  // open: RD0
  Multiplexer #(.Selector_Bits(2), .Bits(32)) multiplexer_1 (
    .sel(alu_asel), .in_0(R_rs1), .in_1(pc), .in_2({32{1'b0}}), .in_3({32{1'b0}}), .out(multiplexer_1_out));
  // RV5_ALU rv5_alu_1: pin names not known; wires that end beside it: multiplexer_1_out, rv5_alu_1_p2, alu_op, rv5_pcu_1_p4, rv5_alu_1_p5, rv5_alu_1_p6, rv5_alu_1_p7
  Multiplexer #(.Bits(32)) multiplexer_2 (.sel(alu_bsel), .in_0(rv5_gpr_1_rb), .in_1(rv5_pcu_1_p6), .out(rv5_alu_1_p2));
  RV5_BRANCH_COND_GEN rv5_branch_cond_gen_1 (
    .carry(rv5_alu_1_p5), .eq(rv5_alu_1_p6), .slt(rv5_alu_1_p7), .funct3(funct3), .branch_sel(branch_sel),
    .jal_sel(jal_sel), .br_jmp(rv5_pcu_1_p5));
  // RV5_MEMORY rv5_memory_1: pin names not known; wires that end beside it: pc, rv5_pcu_1_p4, memwen_t, memren, clock, mem_b, mem_h, ld_signext, dm_mem_addr, dm_mem_wen, dm_mem_wdata, rv5_gpr_1_rb, {funct12, rs1, funct3, rd, opcode}, rv5_memory_1_p14, dm_mem_rdata
  Add #(.Bits(30)) add_1 (.a(pc[31:2]), .b({30{1'b0}}), .c_i(1'b1), .s(add_1_s));  // open: c_o
  Multiplexer #(.Selector_Bits(2), .Bits(32)) multiplexer_3 (
    .sel(wb_sel), .in_0(rv5_pcu_1_p4), .in_1({add_1_s, 2'b00}), .in_2(rv5_memory_1_p14), .in_3({32{1'b0}}),
    .out(wb));

  // Other names for the same wires on the sheet: clk = clock

  // Notes on the sheet:
  //   clock: Hz: 5000
  //   TODO: 
  //   scrap pipeline stage division - done
  //   R_rs1 & R_rs2 - done
  //   op1 & op2 for ALU instead of mod - done
  //   tri-state for one-hot mux - done
  //   PCU simplify: branch condition in control logic - done
  //   alu_asel = 2 -> Can be done via r0? - No, we would need a mux to select rs1,
  //   so we would just be moving the mux somewhere else.
  //   Startup script
  //   Debug sep - done
  //   RV5-PROCESSOR
  //   Note: In the debug module I have
  //   something set up to override
  //   this clock to maximum when debug
  //   work needs to be done.
  //   It's definitely a hack but worth it
  //   for the debugging performance.
  //   So the clock speed that you set 
  //   here really just dictates how 
  //   fast it will go *most* of the time.
  //   (Unless you disable that feature.)
  //   This is a Von Neumann design, so pc runs along the top
  //   to the shared RV5-MEMORY block and inst comes back the
  //   same way. A Harvard-style CPU would have separate instruction
  //   memory instead.
  //   An alternate way to implement a Von Neumann architecture is to 
  //   have a fetch/execute cycle, where one clock tick is spent reading the
  //   instruction from memory and the next is spent executing it.
  //   RALU
  //   About the CPU
  //   This is a single-cycle RV32I processor. In addition to the base instruction set, it also implements
  //   the Ziscr extension and contains a debug module.
  //   Additionally, this is a Von Neumann architecture, and so instruction memory and data memory are
  //   merged. This makes it look slightly different than some educational datapath diagrams you might
  //   see, which sometimes show the Harvard style.
endmodule
